// Logisim project CombinationalMultiplier.circ as structural Verilog: 1 circuit, main circuit main
module main (
  input  SignedMode,
  input  A3,
  input  A2,
  input  A1,
  input  A0,
  input  B3,
  input  B2,
  input  B1,
  input  B0,
  output Prdct7,
  output Prdct6,
  output Prdct5,
  output Prdct4,
  output Prdct3,
  output Prdct2,
  output Prdct1,
  output Prdct0
);

  wire and_1_out, and_2_out, and_3_out, carrylookaheadadder_1_p7, carrylookaheadadder_1_p9,
       carrylookaheadadder_1_p11, carrylookaheadadder_1_p13, carrylookaheadadder_2_p9,
       carrylookaheadadder_2_p11, fourbitstwotoonemux_1_p7, fourbitstwotoonemux_1_p9,
       fourbitstwotoonemux_1_p11, fourbitstwotoonemux_1_p13, fourbitstwotoonemux_1_p14,
       fourbitstwotoonemux_1_p15, fourbitstwotoonemux_2_p5, fourbitstwotoonemux_2_p7,
       fourbitstwotoonemux_2_p9, fourbitstwotoonemux_2_p11, onemoreeightbitsclaadder_1_p1,
       onemoreeightbitsclaadder_1_p2, onemoreeightbitsclaadder_1_p3, onemoreeightbitsclaadder_1_p4,
       onemoreeightbitsclaadder_1_p7, onemoreeightbitsclaadder_1_p9, onemoreeightbitsclaadder_1_p11,
       onemoreeightbitsclaadder_1_p13, onemoreeightbitsclaadder_1_p15, onemoreeightbitsclaadder_1_p17,
       onemoreeightbitsclaadder_1_p19, onemoreeightbitsclaadder_1_p21, partialproductgenerator_1_p1,
       partialproductgenerator_1_p2, partialproductgenerator_1_p3, partialproductgenerator_1_p4,
       partialproductgenerator_1_p5, partialproductgenerator_1_p7, partialproductgenerator_1_p9,
       partialproductgenerator_1_p11, partialproductgenerator_1_p13, partialproductgenerator_1_p15,
       partialproductgenerator_1_p17, partialproductgenerator_1_p19, partialproductgenerator_1_p21,
       partialproductsummator_1_p2, partialproductsummator_1_p3, partialproductsummator_1_p14,
       selectchain8bitsmux_1_p1, selectchain8bitsmux_1_p3, selectchain8bitsmux_1_p5,
       selectchain8bitsmux_1_p9, xor_1_out;

  and and_1 (and_1_out, A3, SignedMode);
  xor xor_1 (xor_1_out, A3, B3);
  and and_2 (and_2_out, SignedMode, xor_1_out);
  and and_3 (and_3_out, SignedMode, B3);
  // OneMoreEightBitsCLAadder onemoreeightbitsclaadder_1: pin names not known; wires that end beside it: onemoreeightbitsclaadder_1_p1, onemoreeightbitsclaadder_1_p2, onemoreeightbitsclaadder_1_p3, onemoreeightbitsclaadder_1_p4, 1'b0, 1'b1, onemoreeightbitsclaadder_1_p7, 1'b0, onemoreeightbitsclaadder_1_p9, 1'b0, onemoreeightbitsclaadder_1_p11, 1'b0, onemoreeightbitsclaadder_1_p13, 1'b0, onemoreeightbitsclaadder_1_p15, 1'b0, onemoreeightbitsclaadder_1_p17, 1'b0, onemoreeightbitsclaadder_1_p19, 1'b0, onemoreeightbitsclaadder_1_p21, and_2_out, onemoreeightbitsclaadder_1_p21, onemoreeightbitsclaadder_1_p7, onemoreeightbitsclaadder_1_p9, onemoreeightbitsclaadder_1_p11, onemoreeightbitsclaadder_1_p13, onemoreeightbitsclaadder_1_p15, onemoreeightbitsclaadder_1_p17, onemoreeightbitsclaadder_1_p19
  // CarryLookaheadAdder carrylookaheadadder_1: pin names not known; wires that end beside it: 1'b0, A3, 1'b0, A2, A1, 1'b0, carrylookaheadadder_1_p7, A0, carrylookaheadadder_1_p9, 1'b0, carrylookaheadadder_1_p11, 1'b1, carrylookaheadadder_1_p13, 1'b0, B3
  // FourBitsTwoToOneMUX fourbitstwotoonemux_1: pin names not known; wires that end beside it: carrylookaheadadder_1_p7, carrylookaheadadder_1_p9, carrylookaheadadder_1_p11, carrylookaheadadder_1_p13, and_1_out, A3, fourbitstwotoonemux_1_p7, A2, fourbitstwotoonemux_1_p9, A1, fourbitstwotoonemux_1_p11, A0, fourbitstwotoonemux_1_p13, fourbitstwotoonemux_1_p14, fourbitstwotoonemux_1_p15
  // CarryLookaheadAdder carrylookaheadadder_2: pin names not known; wires that end beside it: 1'b0, B2, B1, 1'b0, fourbitstwotoonemux_1_p14, B0, fourbitstwotoonemux_1_p15, 1'b0, carrylookaheadadder_2_p9, 1'b1, carrylookaheadadder_2_p11
  // FourBitsTwoToOneMUX fourbitstwotoonemux_2: pin names not known; wires that end beside it: carrylookaheadadder_2_p9, carrylookaheadadder_2_p11, and_3_out, B3, fourbitstwotoonemux_2_p5, B2, fourbitstwotoonemux_2_p7, B1, fourbitstwotoonemux_2_p9, B0, fourbitstwotoonemux_2_p11
  // SelectChain8bitsMUX selectchain8bitsmux_1: pin names not known; wires that end beside it: selectchain8bitsmux_1_p1, Prdct7, selectchain8bitsmux_1_p3, Prdct6, selectchain8bitsmux_1_p5, Prdct5, onemoreeightbitsclaadder_1_p1, Prdct4, selectchain8bitsmux_1_p9, Prdct3, onemoreeightbitsclaadder_1_p2, Prdct2, onemoreeightbitsclaadder_1_p3, Prdct1, onemoreeightbitsclaadder_1_p4, Prdct0
  // PartialProductGenerator partialproductgenerator_1: pin names not known; wires that end beside it: partialproductgenerator_1_p1, partialproductgenerator_1_p2, partialproductgenerator_1_p3, partialproductgenerator_1_p4, partialproductgenerator_1_p5, fourbitstwotoonemux_2_p11, partialproductgenerator_1_p7, fourbitstwotoonemux_2_p9, partialproductgenerator_1_p9, fourbitstwotoonemux_2_p7, partialproductgenerator_1_p11, fourbitstwotoonemux_2_p5, partialproductgenerator_1_p13, fourbitstwotoonemux_1_p13, partialproductgenerator_1_p15, fourbitstwotoonemux_1_p11, partialproductgenerator_1_p17, fourbitstwotoonemux_1_p9, partialproductgenerator_1_p19, fourbitstwotoonemux_1_p7, partialproductgenerator_1_p21
  // PartialProductSummator partialproductsummator_1: pin names not known; wires that end beside it: partialproductgenerator_1_p19, partialproductsummator_1_p2, partialproductsummator_1_p3, partialproductgenerator_1_p4, partialproductgenerator_1_p11, partialproductgenerator_1_p17, onemoreeightbitsclaadder_1_p4, partialproductgenerator_1_p7, onemoreeightbitsclaadder_1_p3, partialproductgenerator_1_p13, onemoreeightbitsclaadder_1_p2, partialproductgenerator_1_p3, selectchain8bitsmux_1_p9, partialproductsummator_1_p14, onemoreeightbitsclaadder_1_p1, partialproductgenerator_1_p2, selectchain8bitsmux_1_p5, partialproductgenerator_1_p15, selectchain8bitsmux_1_p3, partialproductgenerator_1_p1, selectchain8bitsmux_1_p1
endmodule
