// Logisim project SequentialMultiplier.circ as structural Verilog: 1 circuit, main circuit main
module main (
  input  SignedMode,
  input  B3,
  input  B2,
  input  B1,
  input  B0,
  input  START,
  input  A3,
  input  A2,
  input  A1,
  input  A0,
  input  Reset,
  output Prod7,
  output Prod6,
  output Prod5,
  output Prod4,
  output Prod3,
  output Prod2,
  output Prod1,
  output Prod0,
  output DONE,
  output BUSY
);

  wire and_1_out, and_2_out, and_3_out, carrylookaheadadder_1_p2, carrylookaheadadder_1_p4,
       carrylookaheadadder_1_p6, carrylookaheadadder_1_p8, carrylookaheadadder_1_p24,
       carrylookaheadadder_2_p2, carrylookaheadadder_2_p4, carrylookaheadadder_2_p6, clock_1_out,
       controllerfsm_1_p6, eightbitsaddorzeromux_1_p1, eightbitsaddorzeromux_1_p2,
       eightbitsaddorzeromux_1_p4, eightbitsaddorzeromux_1_p7, eightbitsaddorzeromux_1_p8,
       eightbitsaddorzeromux_1_p11, eightbitsaddorzeromux_1_p13, eightbitsaddorzeromux_1_p15,
       eightbitsaddorzeromux_1_p17, eightbitsaddorzeromux_1_p19, eightbitsaddorzeromux_1_p20,
       eightbitsaddorzeromux_1_p21, eightbitsaddorzeromux_1_p22, eightbitsclaadder_1_p1,
       eightbitsclaadder_1_p2, eightbitsclaadder_1_p3, eightbitsclaadder_1_p4, eightbitsclaadder_1_p5,
       eightbitsclaadder_1_p6, eightbitsclaadder_1_p7, eightbitsclaadder_1_p8, eightbitsclaadder_1_p9,
       eightbitsclaadder_1_p10, eightbitsclaadder_1_p11, fourbitsrightshiftregister_1_p1,
       fourbitsrightshiftregister_1_p7, fourbitstwotoonemux_1_p1, fourbitstwotoonemux_1_p2,
       fourbitstwotoonemux_1_p3, fourbitstwotoonemux_1_p4, fourbitstwotoonemux_1_p5,
       fourbitstwotoonemux_1_p6, multiplicandleftshiftregister_1_p5, multiplicandleftshiftregister_1_p7,
       multiplicandleftshiftregister_1_p8, multiplicandleftshiftregister_1_p10,
       multiplicandleftshiftregister_1_p11, multiplicandleftshiftregister_1_p13,
       multiplicandleftshiftregister_1_p14, multiplicandleftshiftregister_1_p16,
       multiplicandleftshiftregister_1_p17, multiplicandleftshiftregister_1_p18,
       multiplicandleftshiftregister_1_p21, not_1_out, onemoreeightbitsclaadder_1_p7,
       onemoreeightbitsclaadder_1_p9, onemoreeightbitsclaadder_1_p11, onemoreeightbitsclaadder_1_p13,
       onemoreeightbitsclaadder_1_p15, onemoreeightbitsclaadder_1_p17, onemoreeightbitsclaadder_1_p19,
       onemoreeightbitsclaadder_1_p21, or_1_out, twobitscounter_1_p4, xor_1_out;

  and and_1 (and_1_out, A3, SignedMode);
  xor xor_1 (xor_1_out, A3, B3);
  and and_2 (and_2_out, SignedMode, B3);
  and and_3 (and_3_out, SignedMode, xor_1_out);
  Clock clock_1 (.out(clock_1_out));
  // CarryLookaheadAdder carrylookaheadadder_1: pin names not known; wires that end beside it: 1'b0, carrylookaheadadder_1_p2, A3, carrylookaheadadder_1_p4, 1'b0, carrylookaheadadder_1_p6, A2, carrylookaheadadder_1_p8, A1, and_1_out, 1'b0, carrylookaheadadder_1_p2, A3, A0, carrylookaheadadder_1_p4, A2, 1'b0, carrylookaheadadder_1_p6, A1, 1'b1, carrylookaheadadder_1_p8, A0, 1'b0, carrylookaheadadder_1_p24
  // FourBitsTwoToOneMUX fourbitstwotoonemux_1: pin names not known; wires that end beside it: fourbitstwotoonemux_1_p1, fourbitstwotoonemux_1_p2, fourbitstwotoonemux_1_p3, fourbitstwotoonemux_1_p4, fourbitstwotoonemux_1_p5, fourbitstwotoonemux_1_p6
  // MultiplicandLeftShiftRegister multiplicandleftshiftregister_1: pin names not known; wires that end beside it: fourbitstwotoonemux_1_p4, fourbitstwotoonemux_1_p3, fourbitstwotoonemux_1_p2, fourbitstwotoonemux_1_p1, multiplicandleftshiftregister_1_p5, 1'b0, multiplicandleftshiftregister_1_p7, multiplicandleftshiftregister_1_p8, 1'b0, multiplicandleftshiftregister_1_p10, multiplicandleftshiftregister_1_p11, 1'b0, multiplicandleftshiftregister_1_p13, multiplicandleftshiftregister_1_p14, Reset, multiplicandleftshiftregister_1_p16, multiplicandleftshiftregister_1_p17, multiplicandleftshiftregister_1_p18, multiplicandleftshiftregister_1_p17, multiplicandleftshiftregister_1_p16, multiplicandleftshiftregister_1_p21, multiplicandleftshiftregister_1_p14, multiplicandleftshiftregister_1_p13, clock_1_out, multiplicandleftshiftregister_1_p11, multiplicandleftshiftregister_1_p10, 1'b0, multiplicandleftshiftregister_1_p8, multiplicandleftshiftregister_1_p7
  // EightBitsAddOrZeroMUX eightbitsaddorzeromux_1: pin names not known; wires that end beside it: eightbitsaddorzeromux_1_p1, eightbitsaddorzeromux_1_p2, eightbitsaddorzeromux_1_p2, eightbitsaddorzeromux_1_p4, eightbitsaddorzeromux_1_p4, eightbitsaddorzeromux_1_p1, eightbitsaddorzeromux_1_p7, eightbitsaddorzeromux_1_p8, eightbitsaddorzeromux_1_p8, eightbitsaddorzeromux_1_p7, eightbitsaddorzeromux_1_p11, eightbitsaddorzeromux_1_p11, eightbitsaddorzeromux_1_p13, eightbitsaddorzeromux_1_p13, eightbitsaddorzeromux_1_p15, eightbitsaddorzeromux_1_p15, eightbitsaddorzeromux_1_p17, 1'b0, eightbitsaddorzeromux_1_p19, eightbitsaddorzeromux_1_p20, eightbitsaddorzeromux_1_p21, eightbitsaddorzeromux_1_p22
  // EightBitsCLAadder eightbitsclaadder_1: pin names not known; wires that end beside it: eightbitsclaadder_1_p1, eightbitsclaadder_1_p2, eightbitsclaadder_1_p3, eightbitsclaadder_1_p4, eightbitsclaadder_1_p5, eightbitsclaadder_1_p6, eightbitsclaadder_1_p7, eightbitsclaadder_1_p8, eightbitsclaadder_1_p9, eightbitsclaadder_1_p10, eightbitsclaadder_1_p11
  // FourBitsRightShiftRegister fourbitsrightshiftregister_1: pin names not known; wires that end beside it: fourbitsrightshiftregister_1_p1, multiplicandleftshiftregister_1_p18, multiplicandleftshiftregister_1_p21, multiplicandleftshiftregister_1_p5, Reset, clock_1_out, fourbitsrightshiftregister_1_p7
  // CarryLookaheadAdder carrylookaheadadder_2: pin names not known; wires that end beside it: B3, carrylookaheadadder_2_p2, 1'b0, carrylookaheadadder_2_p4, B2, carrylookaheadadder_2_p6, B1, and_2_out, 1'b0, carrylookaheadadder_1_p24, B3, B0, carrylookaheadadder_2_p2, B2, 1'b0, carrylookaheadadder_2_p4, B1, 1'b1, carrylookaheadadder_2_p6, B0
  // FourBitsTwoToOneMUX fourbitstwotoonemux_2: pin names not known; wires that end beside it: fourbitsrightshiftregister_1_p7, fourbitsrightshiftregister_1_p1, fourbitstwotoonemux_1_p6, fourbitstwotoonemux_1_p5, clock_1_out
  // TwoBitsCounter twobitscounter_1: pin names not known; wires that end beside it: Reset, multiplicandleftshiftregister_1_p21, multiplicandleftshiftregister_1_p18, twobitscounter_1_p4
  not not_1 (not_1_out, twobitscounter_1_p4);
  or or_1 (or_1_out, multiplicandleftshiftregister_1_p21, multiplicandleftshiftregister_1_p18);
  // EightBitsAccumulator eightbitsaccumulator_1: pin names not known; wires that end beside it: eightbitsclaadder_1_p3, 1'b0, eightbitsclaadder_1_p2, 1'b0, eightbitsclaadder_1_p1, eightbitsaddorzeromux_1_p19, 1'b0, eightbitsaddorzeromux_1_p17, clock_1_out, eightbitsclaadder_1_p10, Reset, eightbitsclaadder_1_p8, multiplicandleftshiftregister_1_p18, eightbitsclaadder_1_p6, or_1_out, eightbitsaddorzeromux_1_p22, eightbitsclaadder_1_p11, eightbitsaddorzeromux_1_p21, 1'b0, eightbitsaddorzeromux_1_p20
  and and_4 (multiplicandleftshiftregister_1_p18, not_1_out, controllerfsm_1_p6);
  // ControllerFSM controllerfsm_1: pin names not known; wires that end beside it: START, DONE, twobitscounter_1_p4, BUSY, Reset, controllerfsm_1_p6, clock_1_out, multiplicandleftshiftregister_1_p21
  // OneMoreEightBitsCLAadder onemoreeightbitsclaadder_1: pin names not known; wires that end beside it: eightbitsclaadder_1_p6, eightbitsclaadder_1_p10, eightbitsaddorzeromux_1_p17, eightbitsaddorzeromux_1_p19, 1'b0, 1'b1, onemoreeightbitsclaadder_1_p7, 1'b0, onemoreeightbitsclaadder_1_p9, 1'b0, onemoreeightbitsclaadder_1_p11, 1'b0, onemoreeightbitsclaadder_1_p13, 1'b0, onemoreeightbitsclaadder_1_p15, 1'b0, onemoreeightbitsclaadder_1_p17, 1'b0, onemoreeightbitsclaadder_1_p19, 1'b0, onemoreeightbitsclaadder_1_p21
  // SelectChain8bitsMUX selectchain8bitsmux_1: pin names not known; wires that end beside it: onemoreeightbitsclaadder_1_p11, onemoreeightbitsclaadder_1_p13, onemoreeightbitsclaadder_1_p15, onemoreeightbitsclaadder_1_p17, onemoreeightbitsclaadder_1_p19, eightbitsaddorzeromux_1_p20, Prod7, eightbitsaddorzeromux_1_p21, Prod6, eightbitsaddorzeromux_1_p22, Prod5, eightbitsclaadder_1_p6, Prod4, eightbitsclaadder_1_p8, Prod3, eightbitsclaadder_1_p10, Prod2, eightbitsaddorzeromux_1_p17, Prod1, eightbitsaddorzeromux_1_p19, Prod0
endmodule
