// Logisim project SevenBitsDivider_Schematic.circ as structural Verilog: 1 circuit, main circuit Divider_Schematic
module Divider_Schematic (
  input  Dvsr6,
  input  Dvsr5,
  input  Dvsr4,
  input  Dvsr3,
  input  Dvsr2,
  input  Dvsr1,
  input  Dvsr0,
  input  START,
  input  Reset,
  input  Dvdnd6,
  input  Dvdnd5,
  input  Dvdnd4,
  input  Dvdnd3,
  input  Dvdnd2,
  input  Dvdnd1,
  input  Dvdnd0,
  input  SignedMode,
  output ERROR,
  output NegativeQuotient,
  output NegativeRemainder,
  output IDLE,
  output DONE,
  output BUSY,
  output Quo6,
  output Quo5,
  output Quo4,
  output Quo3,
  output Quo2,
  output Quo1,
  output Quo0,
  output Rem6,
  output Rem5,
  output Rem4,
  output Rem3,
  output Rem2,
  output Rem1,
  output Rem0
);

  wire and_1_out, and_2_out, clock_1_out, counter4decimal6_1_p5, divdercontroller_1_p10,
       eightbitsclaadder_1_p7, eightbitsclaadder_1_p9, eightbitsclaadder_1_p11, eightbitsclaadder_1_p13,
       eightbitsclaadder_1_p15, eightbitsclaadder_1_p17, eightbitsclaadder_1_p19, eightbitsclaadder_1_p21,
       eightbitsclaadder_2_p7, eightbitsclaadder_2_p9, eightbitsclaadder_2_p11, eightbitsclaadder_2_p13,
       eightbitsclaadder_2_p15, eightbitsclaadder_2_p17, eightbitsclaadder_2_p19, eightbitsclaadder_2_p21,
       eightbitsregister_1_p3, eightbitsregister_1_p4, eightbitsregister_1_p5, eightbitsregister_1_p7,
       eightbitsregister_1_p9, eightbitsregister_1_p11, eightbitsregister_1_p13, eightbitsregister_1_p15,
       eightbitsregister_1_p17, gecomparator_1_p6, gecomparator_1_p7, gecomparator_1_p8, gecomparator_1_p9,
       gecomparator_1_p10, gecomparator_1_p11, gecomparator_1_p12, gecomparator_1_p13, multiplexer_1_out,
       multiplexer_2_out, multiplexer_3_out, muxfordivisorregister_1_p1, muxfordivisorregister_1_p2,
       muxfordivisorregister_1_p3, muxfordivisorregister_1_p4, muxfordivisorregister_1_p5,
       muxfordivisorregister_1_p7, muxfordivisorregister_1_p9, muxfordivisorregister_1_p10,
       muxfordivisorregister_1_p12, muxfordivisorregister_1_p13, muxfordivisorregister_1_p15,
       muxfordivisorregister_1_p16, muxfordivisorregister_1_p18, muxfordivisorregister_1_p19,
       muxfordivisorregister_1_p21, muxfordivisorregister_1_p22, muxfordivisorregister_1_p24,
       muxfordivisorregister_1_p25, muxfordivisorregister_1_p27, muxfordivisorregister_1_p28,
       muxfordivisorregister_1_p30, muxfordivisorregister_1_p31, muxfordivisorregister_1_p32,
       muxforquotientload_1_p8, muxforquotientload_1_p9, muxforquotientload_1_p11, muxforquotientload_1_p12,
       muxforquotientload_1_p14, muxforquotientload_1_p15, muxforquotientload_1_p17,
       muxforquotientload_1_p18, muxforquotientload_1_p20, muxforquotientload_1_p21,
       muxforquotientload_1_p23, muxforquotientload_1_p24, muxforquotientload_1_p26,
       muxforquotientload_1_p27, muxforquotientsteppath_1_p8, muxforquotientsteppath_1_p10,
       muxforquotientsteppath_1_p12, muxforquotientsteppath_1_p14, muxforquotientsteppath_1_p16,
       muxforquotientsteppath_1_p18, muxforquotientsteppath_1_p20, muxforquotientsteppath_3_p1,
       muxforquotientsteppath_3_p2, muxforquotientsteppath_3_p3, muxforquotientsteppath_3_p4,
       muxforquotientsteppath_3_p5, muxforquotientsteppath_3_p6, muxforquotientsteppath_4_p5,
       muxforquotientsteppath_4_p8, muxforquotientsteppath_4_p10, muxforquotientsteppath_4_p12,
       muxforquotientsteppath_4_p14, muxforquotientsteppath_4_p16, muxforquotientsteppath_4_p18,
       muxforquotientsteppath_4_p20, muxforremainderge_1_p7, muxforremainderge_1_p9, muxforremainderge_1_p11,
       muxforremainderge_1_p13, muxforremainderge_1_p15, muxforremainderge_1_p17, muxforremainderge_1_p19,
       muxforremainderge_1_p21, muxforremainderload_1_p3, muxforremainderload_1_p5, muxforremainderload_1_p7,
       muxforremainderload_1_p9, muxforremainderload_1_p11, muxforremainderload_1_p13,
       muxforshiftedquotient_1_p8, muxforshiftedquotient_1_p10, nor_1_out, not_1_out,
       selectchain8bitsmux_1_p7, selectchain8bitsmux_1_p9, sevenbitsregister_2_p1, sevenbitsregister_2_p2,
       sevenbitsregister_2_p3, sevenbitsregister_2_p4, sevenbitsregister_2_p5, sevenbitsregister_2_p6,
       sevenbitsregister_2_p7, twocomplementsconv_1_p10, twocomplementsconv_1_p12, twocomplementsconv_1_p14,
       twocomplementsconv_1_p16, twocomplementsconv_1_p18, twocomplementsconv_1_p20, twocomplementsconv_2_p2,
       twocomplementsconv_2_p4, twocomplementsconv_2_p6, twocomplementsconv_2_p8, twocomplementsconv_2_p10,
       twocomplementsconv_2_p12, twocomplementsconv_2_p14, twocomplementsconv_2_p16,
       twocomplementsconv_2_p18, twocomplementsconv_2_p20, twocomplementsconv_2_p22,
       twocomplementsconv_2_p24, twocomplementsconv_2_p26, xor_1_out;

  D_Flip_Flop d_ff_1 (
    .D(multiplexer_1_out), .clk(clock_1_out), .Q(NegativeQuotient), .reset(Reset));  // open: Qn, preset
  D_Flip_Flop d_ff_2 (
    .D(multiplexer_2_out), .clk(clock_1_out), .Q(NegativeRemainder), .reset(Reset));  // open: Qn, preset
  Multiplexer multiplexer_1 (
    .in0(NegativeQuotient), .in1(and_2_out), .out(multiplexer_1_out), .sel(muxfordivisorregister_1_p7));
  Multiplexer multiplexer_2 (
    .in0(NegativeRemainder), .in1(and_1_out), .out(multiplexer_2_out), .sel(muxfordivisorregister_1_p7));
  Clock clock_1 (.out(clock_1_out));
  and and_1 (and_1_out, Dvdnd6, SignedMode);
  and and_2 (and_2_out, SignedMode, xor_1_out);
  xor xor_1 (xor_1_out, Dvdnd6, Dvsr6);
  // MUXforDivisorRegister muxfordivisorregister_1: pin names not known; wires that end beside it: muxfordivisorregister_1_p1, muxfordivisorregister_1_p2, muxfordivisorregister_1_p3, muxfordivisorregister_1_p4, muxfordivisorregister_1_p5, clock_1_out, muxfordivisorregister_1_p7, Reset, muxfordivisorregister_1_p9, muxfordivisorregister_1_p10, muxfordivisorregister_1_p10, muxfordivisorregister_1_p12, muxfordivisorregister_1_p13, muxfordivisorregister_1_p13, muxfordivisorregister_1_p15, muxfordivisorregister_1_p16, muxfordivisorregister_1_p16, muxfordivisorregister_1_p18, muxfordivisorregister_1_p19, muxfordivisorregister_1_p19, muxfordivisorregister_1_p21, muxfordivisorregister_1_p22, muxfordivisorregister_1_p22, muxfordivisorregister_1_p24, muxfordivisorregister_1_p25, muxfordivisorregister_1_p25, muxfordivisorregister_1_p27, muxfordivisorregister_1_p28, muxfordivisorregister_1_p28, muxfordivisorregister_1_p30, muxfordivisorregister_1_p31, muxfordivisorregister_1_p32
  // SevenBitsRegister sevenbitsregister_1: pin names not known; wires that end beside it: muxfordivisorregister_1_p12, muxfordivisorregister_1_p15, muxfordivisorregister_1_p18, muxfordivisorregister_1_p21, muxfordivisorregister_1_p24, muxfordivisorregister_1_p27, muxfordivisorregister_1_p9
  // TwoComplementsConv twocomplementsconv_1: pin names not known; wires that end beside it: Dvdnd3, muxfordivisorregister_1_p4, Dvdnd5, muxfordivisorregister_1_p3, Dvsr0, muxfordivisorregister_1_p2, Dvsr1, muxfordivisorregister_1_p1, Dvsr2, twocomplementsconv_1_p10, Dvsr3, twocomplementsconv_1_p12, Dvdnd0, twocomplementsconv_1_p14, Dvdnd1, twocomplementsconv_1_p16, Dvdnd2, twocomplementsconv_1_p18, Dvdnd4, twocomplementsconv_1_p20, Dvsr5, muxfordivisorregister_1_p32, Dvsr6, muxfordivisorregister_1_p31, Dvsr4, muxfordivisorregister_1_p30
  // MUXforQuotientLoad muxforquotientload_1: pin names not known; wires that end beside it: twocomplementsconv_1_p20, twocomplementsconv_1_p18, twocomplementsconv_1_p16, twocomplementsconv_1_p14, clock_1_out, muxfordivisorregister_1_p7, Reset, muxforquotientload_1_p8, muxforquotientload_1_p9, muxforquotientload_1_p9, muxforquotientload_1_p11, muxforquotientload_1_p12, muxforquotientload_1_p12, muxforquotientload_1_p14, muxforquotientload_1_p15, muxforquotientload_1_p15, muxforquotientload_1_p17, muxforquotientload_1_p18, muxforquotientload_1_p18, muxforquotientload_1_p20, muxforquotientload_1_p21, muxforquotientload_1_p21, muxforquotientload_1_p23, muxforquotientload_1_p24, muxforquotientload_1_p24, muxforquotientload_1_p26, muxforquotientload_1_p27, muxforquotientload_1_p27
  // SevenBitsRegister sevenbitsregister_2: pin names not known; wires that end beside it: sevenbitsregister_2_p1, sevenbitsregister_2_p2, sevenbitsregister_2_p3, sevenbitsregister_2_p4, sevenbitsregister_2_p5, sevenbitsregister_2_p6, sevenbitsregister_2_p7
  // GEComparator gecomparator_1: pin names not known; wires that end beside it: muxfordivisorregister_1_p18, muxfordivisorregister_1_p21, muxfordivisorregister_1_p24, muxfordivisorregister_1_p27, sevenbitsregister_2_p7, gecomparator_1_p6, gecomparator_1_p7, gecomparator_1_p8, gecomparator_1_p9, gecomparator_1_p10, gecomparator_1_p11, gecomparator_1_p12, gecomparator_1_p13
  // TwoComplementsConv twocomplementsconv_2: pin names not known; wires that end beside it: sevenbitsregister_2_p3, twocomplementsconv_2_p2, sevenbitsregister_2_p1, twocomplementsconv_2_p4, gecomparator_1_p12, twocomplementsconv_2_p6, gecomparator_1_p11, twocomplementsconv_2_p8, gecomparator_1_p10, twocomplementsconv_2_p10, gecomparator_1_p9, twocomplementsconv_2_p12, sevenbitsregister_2_p6, twocomplementsconv_2_p14, sevenbitsregister_2_p5, twocomplementsconv_2_p16, sevenbitsregister_2_p4, twocomplementsconv_2_p18, sevenbitsregister_2_p2, twocomplementsconv_2_p20, gecomparator_1_p7, twocomplementsconv_2_p22, gecomparator_1_p6, twocomplementsconv_2_p24, gecomparator_1_p8, twocomplementsconv_2_p26
  // MUXforQuotientStepPath muxforquotientsteppath_1: pin names not known; wires that end beside it: twocomplementsconv_2_p22, twocomplementsconv_2_p20, twocomplementsconv_2_p18, twocomplementsconv_2_p16, twocomplementsconv_2_p14, NegativeQuotient, sevenbitsregister_2_p7, muxforquotientsteppath_1_p8, sevenbitsregister_2_p1, muxforquotientsteppath_1_p10, sevenbitsregister_2_p2, muxforquotientsteppath_1_p12, sevenbitsregister_2_p3, muxforquotientsteppath_1_p14, sevenbitsregister_2_p4, muxforquotientsteppath_1_p16, sevenbitsregister_2_p5, muxforquotientsteppath_1_p18, sevenbitsregister_2_p6, muxforquotientsteppath_1_p20, twocomplementsconv_2_p12, twocomplementsconv_2_p10
  // MUXforQuotientStepPath muxforquotientsteppath_2: pin names not known; wires that end beside it: 1'b0, 1'b0, 1'b0, 1'b0, 1'b0, ERROR, muxforquotientsteppath_1_p8, Quo6, muxforquotientsteppath_1_p10, Quo5, muxforquotientsteppath_1_p12, Quo4, muxforquotientsteppath_1_p14, Quo3, muxforquotientsteppath_1_p16, Quo2, muxforquotientsteppath_1_p18, Quo1, muxforquotientsteppath_1_p20, Quo0, 1'b0, 1'b0
  // MUXforQuotientStepPath muxforquotientsteppath_3: pin names not known; wires that end beside it: muxforquotientsteppath_3_p1, muxforquotientsteppath_3_p2, muxforquotientsteppath_3_p3, muxforquotientsteppath_3_p4, muxforquotientsteppath_3_p5, muxforquotientsteppath_3_p6, sevenbitsregister_2_p7, muxforquotientload_1_p8, sevenbitsregister_2_p1, muxforquotientload_1_p11, sevenbitsregister_2_p2, muxforquotientload_1_p14, sevenbitsregister_2_p3, muxforquotientload_1_p17, sevenbitsregister_2_p4, muxforquotientload_1_p20, sevenbitsregister_2_p5, muxforquotientload_1_p23, sevenbitsregister_2_p6, muxforquotientload_1_p26, muxfordivisorregister_1_p7
  and and_3 (muxforquotientsteppath_3_p6, divdercontroller_1_p10, not_1_out);
  // Counter4Decimal6 counter4decimal6_1: pin names not known; wires that end beside it: clock_1_out, Reset, muxfordivisorregister_1_p7, muxforquotientsteppath_3_p6, counter4decimal6_1_p5
  not not_1 (not_1_out, counter4decimal6_1_p5);
  // EightBitsRegister eightbitsregister_1: pin names not known; wires that end beside it: clock_1_out, Reset, eightbitsregister_1_p3, eightbitsregister_1_p4, eightbitsregister_1_p5, gecomparator_1_p6, eightbitsregister_1_p7, gecomparator_1_p7, eightbitsregister_1_p9, gecomparator_1_p8, eightbitsregister_1_p11, gecomparator_1_p9, eightbitsregister_1_p13, gecomparator_1_p10, eightbitsregister_1_p15, gecomparator_1_p11, eightbitsregister_1_p17, gecomparator_1_p12
  // MUXforRemainderLoad muxforremainderload_1: pin names not known; wires that end beside it: eightbitsregister_1_p7, eightbitsregister_1_p9, muxforremainderload_1_p3, eightbitsregister_1_p11, muxforremainderload_1_p5, eightbitsregister_1_p13, muxforremainderload_1_p7, eightbitsregister_1_p15, muxforremainderload_1_p9, eightbitsregister_1_p17, muxforremainderload_1_p11, eightbitsregister_1_p5, muxforremainderload_1_p13, eightbitsregister_1_p3
  // MUXforQuotientStepPath muxforquotientsteppath_4: pin names not known; wires that end beside it: twocomplementsconv_2_p8, twocomplementsconv_2_p6, twocomplementsconv_2_p4, twocomplementsconv_2_p2, muxforquotientsteppath_4_p5, NegativeRemainder, gecomparator_1_p6, muxforquotientsteppath_4_p8, gecomparator_1_p7, muxforquotientsteppath_4_p10, gecomparator_1_p8, muxforquotientsteppath_4_p12, gecomparator_1_p9, muxforquotientsteppath_4_p14, gecomparator_1_p10, muxforquotientsteppath_4_p16, gecomparator_1_p11, muxforquotientsteppath_4_p18, gecomparator_1_p12, muxforquotientsteppath_4_p20
  // MUXforQuotientStepPath muxforquotientsteppath_5: pin names not known; wires that end beside it: 1'b0, 1'b0, 1'b0, 1'b0, 1'b0, ERROR, muxforquotientsteppath_4_p8, Rem6, muxforquotientsteppath_4_p10, Rem5, muxforquotientsteppath_4_p12, Rem4, muxforquotientsteppath_4_p14, Rem3, muxforquotientsteppath_4_p16, Rem2, muxforquotientsteppath_4_p18, Rem1, muxforquotientsteppath_4_p20, Rem0
  // DivderController divdercontroller_1: pin names not known; wires that end beside it: counter4decimal6_1_p5, START, clock_1_out, Reset, Dvsr6, Dvsr5, Dvsr4, BUSY, Dvsr3, divdercontroller_1_p10, Dvsr2, DONE, Dvsr1, muxfordivisorregister_1_p7, Dvsr0, IDLE
  // MUXforShiftedQuotient muxforshiftedquotient_1: pin names not known; wires that end beside it: sevenbitsregister_2_p2, sevenbitsregister_2_p3, sevenbitsregister_2_p4, sevenbitsregister_2_p5, sevenbitsregister_2_p6, gecomparator_1_p13, sevenbitsregister_2_p1, muxforshiftedquotient_1_p8, sevenbitsregister_2_p2, muxforshiftedquotient_1_p10, sevenbitsregister_2_p3, muxforquotientsteppath_3_p1, sevenbitsregister_2_p4, muxforquotientsteppath_3_p2, sevenbitsregister_2_p5, muxforquotientsteppath_3_p3, sevenbitsregister_2_p6, muxforquotientsteppath_3_p4, 1'b0, muxforquotientsteppath_3_p5
  nor nor_1 (nor_1_out, Dvsr6, Dvsr5, Dvsr4, Dvsr3, Dvsr2, Dvsr1, Dvsr0);
  D_Flip_Flop d_ff_3 (.D(multiplexer_3_out), .clk(clock_1_out), .Q(ERROR), .reset(Reset));  // open: Qn, preset
  Multiplexer multiplexer_3 (.in0(ERROR), .in1(nor_1_out), .out(multiplexer_3_out), .sel(START));
  // EightBitsCLAadder eightbitsclaadder_1: pin names not known; wires that end beside it: gecomparator_1_p9, gecomparator_1_p11, gecomparator_1_p12, sevenbitsregister_2_p7, muxfordivisorregister_1_p24, 1'b1, eightbitsclaadder_1_p7, muxfordivisorregister_1_p27, eightbitsclaadder_1_p9, 1'b0, eightbitsclaadder_1_p11, muxfordivisorregister_1_p9, eightbitsclaadder_1_p13, muxfordivisorregister_1_p12, eightbitsclaadder_1_p15, muxfordivisorregister_1_p15, eightbitsclaadder_1_p17, muxfordivisorregister_1_p18, eightbitsclaadder_1_p19, muxfordivisorregister_1_p21, eightbitsclaadder_1_p21
  // EightBitsCLAadder eightbitsclaadder_2: pin names not known; wires that end beside it: eightbitsclaadder_1_p13, eightbitsclaadder_1_p15, eightbitsclaadder_1_p17, eightbitsclaadder_1_p19, 1'b0, 1'b0, eightbitsclaadder_2_p7, 1'b1, eightbitsclaadder_2_p9, 1'b0, eightbitsclaadder_2_p11, 1'b0, eightbitsclaadder_2_p13, 1'b0, eightbitsclaadder_2_p15, 1'b0, eightbitsclaadder_2_p17, 1'b0, eightbitsclaadder_2_p19, 1'b0, eightbitsclaadder_2_p21
  // MUXforRemainderGE muxforremainderge_1: pin names not known; wires that end beside it: eightbitsclaadder_2_p13, eightbitsclaadder_2_p15, eightbitsclaadder_2_p17, eightbitsclaadder_2_p19, gecomparator_1_p13, gecomparator_1_p6, muxforremainderge_1_p7, gecomparator_1_p7, muxforremainderge_1_p9, gecomparator_1_p8, muxforremainderge_1_p11, gecomparator_1_p9, muxforremainderge_1_p13, gecomparator_1_p10, muxforremainderge_1_p15, gecomparator_1_p11, muxforremainderge_1_p17, gecomparator_1_p12, muxforremainderge_1_p19, sevenbitsregister_2_p7, muxforremainderge_1_p21
  // SelectChain8bitsMUX selectchain8bitsmux_1: pin names not known; wires that end beside it: muxforremainderge_1_p13, muxforremainderge_1_p15, muxforremainderge_1_p17, muxforremainderge_1_p19, muxforremainderge_1_p21, eightbitsregister_1_p4, selectchain8bitsmux_1_p7, gecomparator_1_p6, selectchain8bitsmux_1_p9, gecomparator_1_p7, muxforremainderload_1_p3, gecomparator_1_p8, muxforremainderload_1_p5, gecomparator_1_p9, muxforremainderload_1_p7, gecomparator_1_p10, muxforremainderload_1_p9, gecomparator_1_p11, muxforremainderload_1_p11, gecomparator_1_p12, muxforremainderload_1_p13
endmodule
