// Logisim project SevenBitsIntegerSquareRoot_Schematic.circ as structural Verilog: 1 circuit, main circuit SevenBitsIntSQRT
module SevenBitsIntSQRT (
  input  R6,
  input  R5,
  input  R4,
  input  R3,
  input  R2,
  input  R1,
  input  R0,
  output sqrt3,
  output sqrt2,
  output sqrt1,
  output sqrt0,
  output Rem6,
  output Rem5,
  output Rem4,
  output Rem3,
  output Rem2,
  output Rem1,
  output Rem0
);

  wire inputpadder_1_p1, inputpadder_1_p4, inputpadder_1_p7, inputpadder_1_p10, inputpadder_1_p13,
       inputpadder_1_p16, inputpadder_1_p19, inputpadder_1_p22, integersqrtstage_1_p1, integersqrtstage_1_p2,
       integersqrtstage_1_p3, integersqrtstage_1_p6, integersqrtstage_1_p8, integersqrtstage_1_p10,
       integersqrtstage_1_p12, integersqrtstage_1_p14, integersqrtstage_1_p16, integersqrtstage_1_p18,
       integersqrtstage_1_p20, integersqrtstage_2_p2, integersqrtstage_2_p4, integersqrtstage_2_p5,
       integersqrtstage_2_p6, integersqrtstage_2_p10, integersqrtstage_2_p12, integersqrtstage_2_p14,
       integersqrtstage_2_p16, integersqrtstage_2_p18, integersqrtstage_2_p20, integersqrtstage_2_p22,
       integersqrtstage_2_p24, integersqrtstage_3_p2, integersqrtstage_3_p4, integersqrtstage_3_p5,
       integersqrtstage_3_p6, integersqrtstage_3_p10, integersqrtstage_3_p12, integersqrtstage_3_p14,
       integersqrtstage_3_p16, integersqrtstage_3_p18, integersqrtstage_3_p20, integersqrtstage_3_p22,
       integersqrtstage_3_p24, integersqrtstage_4_p5, radicandpairsplitter_1_p1, radicandpairsplitter_1_p2,
       radicandpairsplitter_1_p3, radicandpairsplitter_1_p4, radicandpairsplitter_1_p5,
       radicandpairsplitter_1_p6, radicandpairsplitter_1_p7, radicandpairsplitter_1_p8;

  // InputPadder inputpadder_1: pin names not known; wires that end beside it: inputpadder_1_p1, inputpadder_1_p1, R0, inputpadder_1_p4, inputpadder_1_p4, R1, inputpadder_1_p7, inputpadder_1_p7, R2, inputpadder_1_p10, inputpadder_1_p10, R3, inputpadder_1_p13, inputpadder_1_p13, R4, inputpadder_1_p16, inputpadder_1_p16, R5, inputpadder_1_p19, inputpadder_1_p19, R6, inputpadder_1_p22, inputpadder_1_p22
  // RadicandPairSplitter radicandpairsplitter_1: pin names not known; wires that end beside it: radicandpairsplitter_1_p1, radicandpairsplitter_1_p2, radicandpairsplitter_1_p3, radicandpairsplitter_1_p4, radicandpairsplitter_1_p5, radicandpairsplitter_1_p6, radicandpairsplitter_1_p7, radicandpairsplitter_1_p8
  // integerSQRTstage integersqrtstage_1: pin names not known; wires that end beside it: integersqrtstage_1_p1, integersqrtstage_1_p2, integersqrtstage_1_p3, 1'b0, 1'b0, integersqrtstage_1_p6, 1'b0, integersqrtstage_1_p8, 1'b0, integersqrtstage_1_p10, 1'b0, integersqrtstage_1_p12, 1'b0, integersqrtstage_1_p14, 1'b0, integersqrtstage_1_p16, radicandpairsplitter_1_p8, integersqrtstage_1_p18, radicandpairsplitter_1_p7, integersqrtstage_1_p20
  // integerSQRTstage integersqrtstage_2: pin names not known; wires that end beside it: integersqrtstage_1_p2, integersqrtstage_2_p2, integersqrtstage_1_p1, integersqrtstage_2_p4, integersqrtstage_2_p5, integersqrtstage_2_p6, integersqrtstage_1_p6, integersqrtstage_1_p8, integersqrtstage_1_p10, integersqrtstage_2_p10, integersqrtstage_1_p12, integersqrtstage_2_p12, integersqrtstage_1_p14, integersqrtstage_2_p14, integersqrtstage_1_p16, integersqrtstage_2_p16, integersqrtstage_1_p18, integersqrtstage_2_p18, integersqrtstage_1_p20, integersqrtstage_2_p20, radicandpairsplitter_1_p6, integersqrtstage_2_p22, radicandpairsplitter_1_p5, integersqrtstage_2_p24
  // integerSQRTstage integersqrtstage_3: pin names not known; wires that end beside it: integersqrtstage_2_p4, integersqrtstage_3_p2, integersqrtstage_2_p2, integersqrtstage_3_p4, integersqrtstage_3_p5, integersqrtstage_3_p6, integersqrtstage_2_p10, integersqrtstage_2_p12, integersqrtstage_2_p14, integersqrtstage_3_p10, integersqrtstage_2_p16, integersqrtstage_3_p12, integersqrtstage_2_p18, integersqrtstage_3_p14, integersqrtstage_2_p20, integersqrtstage_3_p16, integersqrtstage_2_p22, integersqrtstage_3_p18, integersqrtstage_2_p24, integersqrtstage_3_p20, radicandpairsplitter_1_p4, integersqrtstage_3_p22, radicandpairsplitter_1_p3, integersqrtstage_3_p24
  // integerSQRTstage integersqrtstage_4: pin names not known; wires that end beside it: integersqrtstage_3_p4, sqrt2, integersqrtstage_3_p2, sqrt1, integersqrtstage_4_p5, sqrt0, integersqrtstage_3_p10, integersqrtstage_3_p12, integersqrtstage_3_p14, integersqrtstage_3_p16, Rem6, integersqrtstage_3_p18, Rem5, integersqrtstage_3_p20, Rem4, integersqrtstage_3_p22, Rem3, integersqrtstage_3_p24, Rem2, radicandpairsplitter_1_p2, Rem1, radicandpairsplitter_1_p1, Rem0
endmodule
