// Logisim project TwosComplementConv_SchematicPartOne.circ as structural Verilog: 1 circuit, main circuit TwoComplementsConv
module TwoComplementsConv (
  input  Dvsr4,
  input  Dvsr6,
  input  Dvsr5,
  input  Dvdnd4,
  input  Dvdnd2,
  input  Dvdnd1,
  input  Dvdnd0,
  input  Dvsr3,
  input  Dvsr2,
  input  Dvsr1,
  input  Dvsr0,
  input  Dvdnd5,
  input  Dvdnd3,
  input  Dvdnd6,
  input  SignedMode,
  output Dvd6,
  output Dvd5,
  output Dvd4,
  output Dvd3,
  output Dvd2,
  output Dvd1,
  output Dvd0,
  output Dvs6,
  output Dvs5,
  output Dvs4,
  output Dvs3,
  output Dvs2,
  output Dvs1,
  output Dvs0
);

  wire and_1_out, and_2_out, eightbitsclaadder_1_p7, eightbitsclaadder_1_p9, eightbitsclaadder_1_p11,
       eightbitsclaadder_1_p13, eightbitsclaadder_1_p15, eightbitsclaadder_1_p17, eightbitsclaadder_1_p19,
       eightbitsclaadder_2_p7, eightbitsclaadder_2_p9, eightbitsclaadder_2_p11, eightbitsclaadder_2_p13,
       eightbitsclaadder_2_p15, eightbitsclaadder_2_p17, eightbitsclaadder_2_p19;

  and and_1 (and_1_out, Dvsr6, SignedMode);
  and and_2 (and_2_out, SignedMode, Dvdnd6);
  // EightBitsCLAadder eightbitsclaadder_1: pin names not known; wires that end beside it: Dvdnd4, Dvdnd2, Dvdnd1, Dvdnd0, 1'b0, 1'b1, eightbitsclaadder_1_p7, 1'b0, eightbitsclaadder_1_p9, 1'b0, eightbitsclaadder_1_p11, 1'b0, eightbitsclaadder_1_p13, 1'b0, eightbitsclaadder_1_p15, 1'b0, eightbitsclaadder_1_p17, 1'b0, eightbitsclaadder_1_p19, 1'b0
  // SevenBitsTwoToOneMUX sevenbitstwotoonemux_1: pin names not known; wires that end beside it: eightbitsclaadder_1_p11, eightbitsclaadder_1_p13, eightbitsclaadder_1_p15, eightbitsclaadder_1_p17, eightbitsclaadder_1_p19, and_2_out, Dvdnd6, Dvd6, Dvdnd5, Dvd5, Dvdnd4, Dvd4, Dvdnd3, Dvd3, Dvdnd2, Dvd2, Dvdnd1, Dvd1, Dvdnd0, Dvd0
  // EightBitsCLAadder eightbitsclaadder_2: pin names not known; wires that end beside it: Dvsr4, Dvsr2, Dvsr1, Dvsr0, 1'b0, 1'b1, eightbitsclaadder_2_p7, 1'b0, eightbitsclaadder_2_p9, 1'b0, eightbitsclaadder_2_p11, 1'b0, eightbitsclaadder_2_p13, 1'b0, eightbitsclaadder_2_p15, 1'b0, eightbitsclaadder_2_p17, 1'b0, eightbitsclaadder_2_p19, 1'b0
  // SevenBitsTwoToOneMUX sevenbitstwotoonemux_2: pin names not known; wires that end beside it: eightbitsclaadder_2_p11, eightbitsclaadder_2_p13, eightbitsclaadder_2_p15, eightbitsclaadder_2_p17, eightbitsclaadder_2_p19, and_1_out, Dvsr6, Dvs6, Dvsr5, Dvs5, Dvsr4, Dvs4, Dvsr3, Dvs3, Dvsr2, Dvs2, Dvsr1, Dvs1, Dvsr0, Dvs0
endmodule
