// Logisim project TenBitsCarryLookAheadAdder_Schematic.circ as structural Verilog: 1 circuit, main circuit TenBitsCLAadder
module TenBitsCLAadder (
  input  B2,
  input  B3,
  input  B4,
  input  B5,
  input  B6,
  input  B7,
  input  B8,
  input  B9,
  input  B0,
  input  Sub,
  input  B1,
  input  A0,
  input  A1,
  input  A2,
  input  A4,
  input  A8,
  input  A9,
  input  A3,
  input  A7,
  input  A5,
  input  A6,
  output S8,
  output S9,
  output S7,
  output S0,
  output S1,
  output S2,
  output S3,
  output S4,
  output S5,
  output S6
);

  wire and_1_out, and_2_out, and_3_out, and_4_out, and_5_out, and_6_out, and_7_out, and_8_out, and_9_out,
       and_10_out, and_11_out, and_12_out, and_13_out, and_14_out, and_15_out, and_16_out, and_17_out,
       and_18_out, and_19_out, and_20_out, and_21_out, and_22_out, and_23_out, and_24_out, and_25_out,
       and_26_out, and_27_out, and_28_out, and_29_out, and_30_out, and_31_out, and_32_out, and_33_out,
       or_1_out, or_2_out, or_3_out, or_4_out, or_5_out, or_6_out, or_7_out, or_8_out, or_9_out, or_10_out,
       or_11_out, or_12_out, or_13_out, or_14_out, or_15_out, xor_1_out, xor_3_out, xor_5_out, xor_6_out,
       xor_8_out, xor_9_out, xor_11_out, xor_12_out, xor_14_out, xor_15_out, xor_17_out, xor_18_out,
       xor_20_out, xor_21_out, xor_23_out, xor_24_out, xor_26_out, xor_27_out, xor_29_out;

  xor xor_1 (xor_1_out, B0, Sub);
  xor xor_2 (S0, A0, xor_1_out);
  and and_1 (and_1_out, A0, xor_1_out);
  xor xor_3 (xor_3_out, B1, Sub);
  xor xor_4 (S1, xor_5_out, and_1_out);
  xor xor_5 (xor_5_out, A1, xor_3_out);
  and and_2 (and_2_out, A1, xor_3_out);
  and and_3 (and_3_out, and_1_out, xor_5_out);
  or or_1 (or_1_out, and_3_out, and_2_out);
  xor xor_6 (xor_6_out, B2, Sub);
  xor xor_7 (S2, xor_8_out, or_1_out);
  and and_4 (and_4_out, A2, xor_6_out);
  xor xor_8 (xor_8_out, A2, xor_6_out);
  and and_5 (and_5_out, and_3_out, xor_8_out);
  xor xor_9 (xor_9_out, B3, Sub);
  and and_6 (and_6_out, xor_8_out, and_2_out);
  or or_2 (or_2_out, and_5_out, and_6_out, and_4_out);
  xor xor_10 (S3, xor_11_out, or_2_out);
  xor xor_11 (xor_11_out, A3, xor_9_out);
  and and_7 (and_7_out, A3, xor_9_out);
  xor xor_12 (xor_12_out, B4, Sub);
  and and_8 (and_8_out, and_6_out, xor_11_out);
  and and_9 (and_9_out, and_5_out, xor_11_out);
  or or_3 (or_3_out, and_8_out, and_9_out, and_11_out);
  or or_4 (or_4_out, or_3_out, and_7_out);
  xor xor_13 (S4, xor_14_out, or_4_out);
  and and_10 (and_10_out, A4, xor_12_out);
  and and_11 (and_11_out, xor_11_out, and_4_out);
  xor xor_14 (xor_14_out, A4, xor_12_out);
  xor xor_15 (xor_15_out, B5, Sub);
  and and_12 (and_12_out, and_9_out, xor_14_out);
  or or_5 (or_5_out, and_12_out, and_14_out);
  xor xor_16 (S5, xor_17_out, or_6_out);
  xor xor_17 (xor_17_out, A5, xor_15_out);
  and and_13 (and_13_out, A5, xor_15_out);
  and and_14 (and_14_out, and_8_out, xor_14_out);
  or or_6 (or_6_out, or_5_out, or_7_out, and_10_out);
  xor xor_18 (xor_18_out, B6, Sub);
  and and_15 (and_15_out, and_11_out, xor_14_out);
  and and_16 (and_16_out, xor_14_out, and_7_out);
  or or_7 (or_7_out, and_15_out, and_16_out);
  xor xor_19 (S6, xor_20_out, or_10_out);
  and and_17 (and_17_out, A6, xor_18_out);
  xor xor_20 (xor_20_out, A6, xor_18_out);
  and and_18 (and_18_out, and_12_out, xor_17_out);
  xor xor_21 (xor_21_out, B7, Sub);
  and and_19 (and_19_out, and_14_out, xor_17_out);
  or or_8 (or_8_out, and_18_out, and_19_out, and_21_out);
  xor xor_22 (S7, xor_23_out, or_13_out);
  xor xor_23 (xor_23_out, A7, xor_21_out);
  and and_20 (and_20_out, A7, xor_21_out);
  and and_21 (and_21_out, and_15_out, xor_17_out);
  or or_9 (or_9_out, and_22_out, and_23_out);
  or or_10 (or_10_out, or_8_out, or_9_out, and_13_out);
  and and_22 (and_22_out, and_16_out, xor_17_out);
  xor xor_24 (xor_24_out, B8, Sub);
  and and_23 (and_23_out, and_10_out, xor_17_out);
  xor xor_25 (S8, xor_26_out, or_15_out);
  and and_24 (and_24_out, A8, xor_24_out);
  xor xor_26 (xor_26_out, A8, xor_24_out);
  and and_25 (and_25_out, xor_26_out, or_15_out);
  or or_11 (or_11_out, and_25_out, and_24_out);
  and and_26 (and_26_out, and_18_out, xor_20_out);
  and and_27 (and_27_out, and_19_out, xor_20_out);
  or or_12 (or_12_out, and_26_out, and_27_out, and_28_out);
  xor xor_27 (xor_27_out, B9, Sub);
  and and_28 (and_28_out, and_21_out, xor_20_out);
  or or_13 (or_13_out, or_12_out, or_14_out, and_17_out);
  xor xor_28 (S9, xor_29_out, or_11_out);
  xor xor_29 (xor_29_out, A9, xor_27_out);
  and and_29 (and_29_out, and_22_out, xor_20_out);
  and and_30 (and_30_out, and_23_out, xor_20_out);
  or or_14 (or_14_out, and_29_out, and_30_out, and_31_out);
  and and_31 (and_31_out, and_13_out, xor_20_out);
  and and_32 (and_32_out, xor_23_out, and_17_out);
  or or_15 (or_15_out, and_32_out, and_33_out, and_20_out);
  and and_33 (and_33_out, xor_23_out, xor_20_out, or_10_out);
endmodule
