// Logisim project TwentyOneBitsCounter_Schematic.circ as structural Verilog: 1 circuit, main circuit TwentyOneBitsCounter
module TwentyOneBitsCounter (
  input  CLK,
  input  Clear,
  input  Reset,
  output cnt0,
  output cnt1,
  output cnt2,
  output cnt3,
  output cnt4,
  output cnt5,
  output cnt6,
  output cnt7,
  output cnt8,
  output cnt9,
  output cnt10,
  output cnt11,
  output cnt12,
  output cnt13,
  output cnt14,
  output cnt15,
  output cnt16,
  output cnt17,
  output cnt18,
  output cnt19,
  output cnt20
);

  wire and_1_out, and_2_out, and_3_out, and_4_out, and_5_out, and_6_out, and_7_out, and_8_out, and_9_out,
       and_10_out, and_11_out, and_12_out, and_13_out, and_14_out, and_15_out, and_16_out, and_17_out,
       and_18_out, and_19_out, dflipflop_1_p4, dflipflop_2_p4, dflipflop_3_p4, dflipflop_4_p4,
       dflipflop_5_p4, dflipflop_6_p4, dflipflop_7_p4, dflipflop_8_p4, dflipflop_9_p4, dflipflop_10_p4,
       dflipflop_11_p4, dflipflop_12_p4, dflipflop_13_p4, dflipflop_14_p4, dflipflop_15_p4, dflipflop_16_p4,
       dflipflop_17_p4, dflipflop_18_p4, dflipflop_19_p4, dflipflop_20_p4, dflipflop_21_p4, or_1_out;

  or or_1 (or_1_out, Clear, Reset);
  // Dflipflop dflipflop_1: pin names not known; wires that end beside it: cnt0, or_1_out, CLK, dflipflop_1_p4
  // Dflipflop dflipflop_2: pin names not known; wires that end beside it: cnt1, or_1_out, CLK, dflipflop_2_p4
  // Dflipflop dflipflop_3: pin names not known; wires that end beside it: cnt2, or_1_out, CLK, dflipflop_3_p4
  // Dflipflop dflipflop_4: pin names not known; wires that end beside it: cnt3, or_1_out, CLK, dflipflop_4_p4
  // Dflipflop dflipflop_5: pin names not known; wires that end beside it: cnt4, or_1_out, CLK, dflipflop_5_p4
  // Dflipflop dflipflop_6: pin names not known; wires that end beside it: cnt5, or_1_out, CLK, dflipflop_6_p4
  // Dflipflop dflipflop_7: pin names not known; wires that end beside it: cnt6, or_1_out, CLK, dflipflop_7_p4
  // Dflipflop dflipflop_8: pin names not known; wires that end beside it: cnt7, or_1_out, CLK, dflipflop_8_p4
  // Dflipflop dflipflop_9: pin names not known; wires that end beside it: cnt8, or_1_out, CLK, dflipflop_9_p4
  // Dflipflop dflipflop_10: pin names not known; wires that end beside it: cnt9, or_1_out, CLK, dflipflop_10_p4
  // Dflipflop dflipflop_11: pin names not known; wires that end beside it: cnt10, or_1_out, CLK, dflipflop_11_p4
  // Dflipflop dflipflop_12: pin names not known; wires that end beside it: cnt11, or_1_out, CLK, dflipflop_12_p4
  // Dflipflop dflipflop_13: pin names not known; wires that end beside it: cnt12, or_1_out, CLK, dflipflop_13_p4
  // Dflipflop dflipflop_14: pin names not known; wires that end beside it: cnt13, or_1_out, CLK, dflipflop_14_p4
  // Dflipflop dflipflop_15: pin names not known; wires that end beside it: cnt14, or_1_out, CLK, dflipflop_15_p4
  // Dflipflop dflipflop_16: pin names not known; wires that end beside it: cnt15, or_1_out, CLK, dflipflop_16_p4
  // Dflipflop dflipflop_17: pin names not known; wires that end beside it: cnt16, or_1_out, CLK, dflipflop_17_p4
  // Dflipflop dflipflop_18: pin names not known; wires that end beside it: cnt17, or_1_out, CLK, dflipflop_18_p4
  // Dflipflop dflipflop_19: pin names not known; wires that end beside it: cnt18, or_1_out, CLK, dflipflop_19_p4
  // Dflipflop dflipflop_20: pin names not known; wires that end beside it: cnt19, or_1_out, CLK, dflipflop_20_p4
  // Dflipflop dflipflop_21: pin names not known; wires that end beside it: cnt20, or_1_out, CLK, dflipflop_21_p4
  not not_1 (cnt0, dflipflop_1_p4);
  xor xor_1 (cnt1, dflipflop_2_p4, cnt0);
  and and_1 (and_1_out, cnt1, cnt0);
  and and_2 (and_2_out, and_1_out, dflipflop_3_p4);
  xor xor_2 (cnt2, dflipflop_3_p4, and_1_out);
  and and_3 (and_3_out, and_2_out, dflipflop_4_p4);
  xor xor_3 (cnt3, and_2_out, dflipflop_4_p4);
  xor xor_4 (cnt4, dflipflop_5_p4, and_3_out);
  and and_4 (and_4_out, and_3_out, dflipflop_5_p4);
  xor xor_5 (cnt5, dflipflop_6_p4, and_4_out);
  and and_5 (and_5_out, and_4_out, dflipflop_6_p4);
  xor xor_6 (cnt6, dflipflop_7_p4, and_5_out);
  and and_6 (and_6_out, and_5_out, dflipflop_7_p4);
  xor xor_7 (cnt7, dflipflop_8_p4, and_6_out);
  and and_7 (and_7_out, and_6_out, dflipflop_8_p4);
  xor xor_8 (cnt8, dflipflop_9_p4, and_7_out);
  and and_8 (and_8_out, and_7_out, dflipflop_9_p4);
  xor xor_9 (cnt9, dflipflop_10_p4, and_8_out);
  and and_9 (and_9_out, and_8_out, dflipflop_10_p4);
  xor xor_10 (cnt10, dflipflop_11_p4, and_9_out);
  and and_10 (and_10_out, and_9_out, dflipflop_11_p4);
  xor xor_11 (cnt11, dflipflop_12_p4, and_10_out);
  and and_11 (and_11_out, and_10_out, dflipflop_12_p4);
  and and_12 (and_12_out, and_11_out, dflipflop_13_p4);
  xor xor_12 (cnt12, dflipflop_13_p4, and_11_out);
  and and_13 (and_13_out, and_12_out, dflipflop_14_p4);
  xor xor_13 (cnt13, dflipflop_14_p4, and_12_out);
  xor xor_14 (cnt14, dflipflop_15_p4, and_13_out);
  and and_14 (and_14_out, and_13_out, dflipflop_15_p4);
  xor xor_15 (cnt15, dflipflop_16_p4, and_14_out);
  and and_15 (and_15_out, and_14_out, dflipflop_16_p4);
  xor xor_16 (cnt16, dflipflop_17_p4, and_15_out);
  and and_16 (and_16_out, and_15_out, dflipflop_17_p4);
  and and_17 (and_17_out, and_16_out, dflipflop_18_p4);
  xor xor_17 (cnt17, dflipflop_18_p4, and_16_out);
  xor xor_18 (cnt18, dflipflop_19_p4, and_17_out);
  and and_18 (and_18_out, and_17_out, dflipflop_19_p4);
  xor xor_19 (cnt19, dflipflop_20_p4, and_18_out);
  and and_19 (and_19_out, and_18_out, dflipflop_20_p4);
  xor xor_20 (cnt20, dflipflop_21_p4, and_19_out);
endmodule
